// Logisim project LC-2200-16.circ as structural Verilog: 5 circuits, main circuit main
module main (
  output [15:0] out_1,
  output [15:0] out_2,
  output [15:0] out_3,
  output [15:0] out_4,
  output [15:0] out_5,
  output [15:0] out_6,
  output [1:0] RegSel,
  output [15:0] out_8,
  output [1:0] func,
  output [15:0] sp,
  output [15:0] out_11,
  output [15:0] out_12,
  output [15:0] out_13,
  output [15:0] out_14,
  output [15:0] out_15,
  output [15:0] out_16
);

  wire clk, comparator_1_eq, DrALU, DrMEM, DrOFF, DrPC, DrREG, LdA, LdB, LdIR, LdMAR, LdPC, LdZ, not_1_out,
       WrMEM, WrREG, Z;
  wire [3:0] Regno;
  wire [15:0] A_q, B_q, bit_extender_1_out, MAR_q, ram_1_data, register_files_1_dataout;

  Clock clock_1 (.out(clk));
  Register #(.width(16)) PC (.D(out_1), .en(LdPC), .Q(out_4), .clk(clk));  // open: clr
  assign out_1 = DrPC ? out_4 : 16'bz;  // Controlled_Buffer controlled_buffer_1
  Comparator #(.width(16)) comparator_1 (.a(out_1), .b({16{1'b0}}), .eq(comparator_1_eq));  // open: gt, lt
  Register #(.width(16)) A (.D(out_1), .en(LdA), .Q(A_q), .clk(clk));  // open: clr
  ALU alu_1 (.A(A_q), .B(B_q), .opcode(func), .\output (out_5));
  assign out_1 = DrALU ? out_5 : 16'bz;  // Controlled_Buffer controlled_buffer_2
  Register #(.width(1)) register_1 (.D(comparator_1_eq), .en(LdZ), .Q(Z), .clk(clk));  // open: clr
  Register #(.width(16)) B (.D(out_1), .en(LdB), .Q(B_q), .clk(clk));  // open: clr
  Register_Files register_files_1 (
    .wrREG(WrREG), .Regno(Regno), .Dataout(register_files_1_dataout), .clk(clk), .Datain(out_1), .v0(out_14),
    .a0(out_12), .t0(out_11), .s0(out_16), .t1(out_13), .t2(out_15), .sp(sp));
  assign out_1 = DrREG ? register_files_1_dataout : 16'bz;  // Controlled_Buffer controlled_buffer_3
  Register #(.width(16)) MAR (.D(out_1), .en(LdMAR), .Q(MAR_q), .clk(clk));  // open: clr
  not not_1 (not_1_out, WrMEM);
  assign out_1 = DrMEM ? ram_1_data : 16'bz;  // Controlled_Buffer controlled_buffer_4
  RAM #(.addrWidth(16), .dataWidth(16), .bus("separate")) ram_1 (
    .addr(MAR_q), .din(out_1), .data(ram_1_data), .str(WrMEM), .clk(clk), .ld(not_1_out));  // open: sel, clr
  Register #(.width(16)) IR (.D(out_1), .en(LdIR), .Q(out_3), .clk(clk));  // open: clr
  assign bit_extender_1_out = {{11{out_3[4]}}, out_3[4:0]};  // Bit_Extender bit_extender_1
  assign out_1 = DrOFF ? bit_extender_1_out : 16'bz;  // Controlled_Buffer controlled_buffer_5
  Microcontrol_unit microcontrol_unit_1 (
    .clk(clk), .DrALU(DrALU), .DrMEM(DrMEM), .DrOFF(DrOFF), .DrPC(DrPC), .DrREG(DrREG), .LdA(LdA), .LdB(LdB),
    .LdIR(LdIR), .LdMAR(LdMAR), .LdPC(LdPC), .LdZ(LdZ), .WrREG(WrREG), .WrMEM(WrMEM), .Regno(Regno),
    .RegSel(RegSel), .\function (func), .Z(Z), .Datain(out_3));

  assign out_2 = out_1;
  assign out_6 = out_1;
  assign out_8 = out_1;

  // Other names for the same wires on the sheet: a0[15:0] = out_12; function[1:0] = func; s0[15:0] = out_16;
  //   t0[15:0] = out_11; t1[15:0] = out_13; t2[15:0] = out_15; v0[15:0] = out_14

  // Notes on the sheet:
  //   SPRING 2016
endmodule

module ALU (
  input  [15:0] A,
  input  [15:0] B,
  input  [1:0] opcode,
  output [15:0] \output 
);

  wire [15:0] adder_1_out, adder_2_out, nand_1_out, subtractor_1_out;

  Adder #(.width(16)) adder_1 (.a(A), .b(B), .out(adder_1_out), .cin(1'b0));  // open: cout
  Subtractor #(.width(16)) subtractor_1 (.a(A), .b(B), .out(subtractor_1_out), .bin(1'b0));  // open: bout
  Adder #(.width(16)) adder_2 (.a(A), .b(16'h1), .out(adder_2_out), .cin(1'b0));  // open: cout
  assign nand_1_out = ~(A & B);  // NAND_Gate nand_1, 16 bits wide
  Multiplexer #(.select(2), .width(16)) multiplexer_1 (
    .in0(adder_1_out), .in1(nand_1_out), .in2(subtractor_1_out), .in3(adder_2_out), .out(\output ),
    .sel(opcode));  // open: en

  // Notes on the sheet:
  //   00 ADD
  //   01 NAND
  //   10 subtract
  //   11 increase by 1
endmodule

module Register_Selector (
  input  weREG,
  input  [3:0] regno,
  output _0,
  output _1,
  output _2,
  output _3,
  output _4,
  output _5,
  output _6,
  output _7,
  output _8,
  output _9,
  output _10,
  output _11,
  output _12,
  output _13,
  output _14,
  output out_18
);

  wire decoder_1_out0, decoder_1_out1, decoder_1_out2, decoder_1_out3, decoder_1_out4, decoder_1_out5,
       decoder_1_out6, decoder_1_out7, decoder_1_out8, decoder_1_out9, decoder_1_out10, decoder_1_out11,
       decoder_1_out12, decoder_1_out13, decoder_1_out14, decoder_1_out15;

  Decoder #(.select(4)) decoder_1 (
    .out0(decoder_1_out0), .out1(decoder_1_out1), .out2(decoder_1_out2), .out3(decoder_1_out3),
    .out4(decoder_1_out4), .out5(decoder_1_out5), .out6(decoder_1_out6), .out7(decoder_1_out7),
    .out8(decoder_1_out8), .out9(decoder_1_out9), .out10(decoder_1_out10), .out11(decoder_1_out11),
    .out12(decoder_1_out12), .out13(decoder_1_out13), .out14(decoder_1_out14), .out15(decoder_1_out15),
    .sel(regno), .en(1'b1));
  and and_1 (_0, decoder_1_out0, weREG);
  and and_2 (_1, decoder_1_out1, weREG);
  and and_3 (_2, decoder_1_out2, weREG);
  and and_4 (_3, decoder_1_out3, weREG);
  and and_5 (_4, decoder_1_out4, weREG);
  and and_6 (_5, decoder_1_out5, weREG);
  and and_7 (_6, decoder_1_out6, weREG);
  and and_8 (_7, decoder_1_out7, weREG);
  and and_9 (_8, decoder_1_out8, weREG);
  and and_10 (_9, decoder_1_out9, weREG);
  and and_11 (_10, decoder_1_out10, weREG);
  and and_12 (_11, decoder_1_out11, weREG);
  and and_13 (_12, decoder_1_out12, weREG);
  and and_14 (_13, decoder_1_out13, weREG);
  and and_15 (_14, decoder_1_out14, weREG);
  and and_16 (out_18, decoder_1_out15, weREG);
endmodule

module Register_Files (
  input  wrREG,
  input  [3:0] Regno,
  input  clk,
  input  [15:0] Datain,
  output [15:0] Dataout,
  output [15:0] v0,
  output [15:0] a0,
  output [15:0] t0,
  output [15:0] t1,
  output [15:0] t2,
  output [15:0] s0,
  output [15:0] sp
);

  wire not_1_out, register_selector_1__0, register_selector_1__1, register_selector_1__2,
       register_selector_1__3, register_selector_1__4, register_selector_1__5, register_selector_1__6,
       register_selector_1__7, register_selector_1__8, register_selector_1__9, register_selector_1__10,
       register_selector_1__11, register_selector_1__12, register_selector_1__13, register_selector_1__14,
       register_selector_1_out_18;
  wire [15:0] _0, _1, _4, _5, _10, _11, _12, _13, _15;

  Register #(.width(16)) register_1 (.D(Datain), .en(register_selector_1__4), .Q(_4), .clk(clk));  // open: clr
  Register #(.width(16)) register_2 (.D(Datain), .en(register_selector_1__3), .Q(a0), .clk(clk));  // open: clr
  Register #(.width(16)) register_3 (.D(Datain), .en(register_selector_1__2), .Q(v0), .clk(clk));  // open: clr
  Register #(.width(16)) register_4 (.D(Datain), .en(register_selector_1__1), .Q(_1), .clk(clk));  // open: clr
  Register #(.width(16)) register_5 (.D({16{1'b0}}), .en(register_selector_1__0), .Q(_0), .clk(clk));  // open: clr
  Register_Selector register_selector_1 (
    .regno(Regno), .weREG(wrREG), ._0(register_selector_1__0), ._1(register_selector_1__1),
    ._2(register_selector_1__2), ._3(register_selector_1__3), ._4(register_selector_1__4),
    ._5(register_selector_1__5), ._6(register_selector_1__6), ._7(register_selector_1__7),
    ._8(register_selector_1__8), ._9(register_selector_1__9), ._10(register_selector_1__10),
    ._11(register_selector_1__11), ._12(register_selector_1__12), ._13(register_selector_1__13),
    ._14(register_selector_1__14), .out_18(register_selector_1_out_18));
  Register #(.width(16)) register_6 (.D(Datain), .en(register_selector_1__9), .Q(s0), .clk(clk));  // open: clr
  Register #(.width(16)) register_7 (.D(Datain), .en(register_selector_1__8), .Q(t2), .clk(clk));  // open: clr
  Register #(.width(16)) register_8 (.D(Datain), .en(register_selector_1__7), .Q(t1), .clk(clk));  // open: clr
  Register #(.width(16)) register_9 (.D(Datain), .en(register_selector_1__6), .Q(t0), .clk(clk));  // open: clr
  Register #(.width(16)) register_10 (.D(Datain), .en(register_selector_1__5), .Q(_5), .clk(clk));  // open: clr
  Register #(.width(16)) register_11 (.D(Datain), .en(register_selector_1__14), .Q(sp), .clk(clk));  // open: clr
  Register #(.width(16)) register_12 (.D(Datain), .en(register_selector_1__13), .Q(_13), .clk(clk));  // open: clr
  Register #(.width(16)) register_13 (.D(Datain), .en(register_selector_1__12), .Q(_12), .clk(clk));  // open: clr
  Register #(.width(16)) register_14 (.D(Datain), .en(register_selector_1__11), .Q(_11), .clk(clk));  // open: clr
  Register #(.width(16)) register_15 (.D(Datain), .en(register_selector_1__10), .Q(_10), .clk(clk));  // open: clr
  not not_1 (not_1_out, wrREG);
  Register #(.width(16)) register_16 (.D(Datain), .en(register_selector_1_out_18), .Q(_15), .clk(clk));  // open: clr
  Multiplexer #(.select(4), .width(16)) multiplexer_1 (
    .in0(_0), .in1(_1), .in2(v0), .in3(a0), .in4(_4), .in5(_5), .in6(t0), .in7(t1), .in8(t2), .in9(s0),
    .in10(_10), .in11(_11), .in12(_12), .in13(_13), .in14(sp), .in15(_15), .out(Dataout), .sel(Regno),
    .en(not_1_out));

  // Other names for the same wires on the sheet: _2[15:0] = v0; _3[15:0] = a0; _6[15:0] = t0; _7[15:0] = t1;
  //   _8[15:0] = t2; _9[15:0] = s0; _14[15:0] = sp
endmodule

module Microcontrol_unit (
  input  clk,
  input  Z,
  input  [15:0] Datain,
  output DrALU,
  output DrMEM,
  output DrOFF,
  output DrPC,
  output DrREG,
  output LdA,
  output LdB,
  output LdIR,
  output LdMAR,
  output LdPC,
  output LdZ,
  output WrREG,
  output WrMEM,
  output [3:0] Regno,
  output [1:0] RegSel,
  output [1:0] \function 
);

  wire [5:0] multiplexer_1_out, rom_2_data, rom_3_data, state_register_q;
  wire [24:0] rom_1_data;

  Register #(.width(6)) state_register (.D(multiplexer_1_out), .Q(state_register_q), .clk(clk));  // open: en, clr
  ROM #(.addrWidth(6), .dataWidth(25)) rom_1 (
    .addr(state_register_q),
    .data({rom_1_data[24:23], \function , RegSel, WrMEM, WrREG, LdZ, LdB, LdA, LdMAR, LdIR, LdPC, DrOFF, DrPC, DrALU, DrMEM, DrREG, rom_1_data[5:0]}));  // open: sel
  Multiplexer #(.select(2), .width(6)) multiplexer_1 (
    .in0(rom_1_data[5:0]), .in1(rom_2_data), .in2(rom_3_data), .out(multiplexer_1_out),
    .sel(rom_1_data[24:23]), .en(1'b1));  // open: in3
  Multiplexer #(.select(2), .width(4)) multiplexer_2 (
    .in0(Datain[12:9]), .in1(Datain[8:5]), .in2(Datain[4:1]), .out(Regno), .sel(RegSel));  // open: in3, en
  ROM #(.addrWidth(3), .dataWidth(6)) rom_2 (.addr(Datain[15:13]), .data(rom_2_data));  // open: sel
  ROM #(.addrWidth(2), .dataWidth(6)) rom_3 (.addr({1'b0, Z}), .data(rom_3_data));  // open: sel

  // Other names for the same wires on the sheet: op[2:0] = Datain[15:13]

  // Notes on the sheet:
  //   main ROM
  //   contents of rom_1 (hex, n*v repeats v):
  //   6201 1082 e00900 84044 108045 20100 84047 8408 20100 8404a 10804b 220100 a020d 840 8404f 8410 2111
  //   20080 84053 8414 2115 40040 4057 88058 410119 1000000 421b 841c 900 1d
  //   Ry
  //   Rz
  //   sequencer
  //   z
  //   Rx
  //   contents of rom_2 (hex, n*v repeats v):
  //   3 9 6 e 12 16 c 1d
  //   contents of rom_3 (hex, n*v repeats v):
  //   0 1a
endmodule
