// Logisim project xie_mingjun.circ as structural Verilog: 13 circuits, main circuit main
module main (
  output [31:0] out_1,
  output [3:0] ex_opcode,
  output [1:0] out_3,
  output [31:0] out_4,
  output [31:0] out_5,
  output [3:0] Ry,
  output [3:0] opcode,
  output [3:0] Rx,
  output [31:0] out_9,
  output [31:0] out_10,
  output [31:0] out_11,
  output [31:0] out_12,
  output [31:0] out_13,
  output [31:0] out_14,
  output [31:0] out_15,
  output [31:0] out_16,
  output [31:0] out_17
);

  wire and_1_out, CLK, comparator_1_eq, comparator_2_eq, comparator_3_eq, comparator_4_lt, comparator_5_eq,
       EN, NoOp, or_2_out, Squash, STALL, take_branch, WB;
  wire [1:0] PC_SELECT;
  wire [3:0] idrr_ex_buffer_1_opcode_out, idrr_ex_buffer_1_rx_in_2, idrr_ex_buffer_1_ry_in_2, OPCODE_MEM,
       OPCODE_WB, REG_WB, REGNO2, Rx_EX, Rx_MEM, Rx_WB, Ry_EX, Ry_MEM, Ry_WB, Rz;
  wire [15:0] Unused;
  wire [23:0] bit_extender_1_out;
  wire [31:0] adder_2_out, idrr_ex_buffer_1_offset_out, idrr_ex_buffer_1_pc_out, idrr_ex_buffer_1_rdata1out,
       idrr_ex_buffer_1_rdata2out, if_idrr_buffer_1_inst_out, mem_wb_buffer_1_ram_out_2, multiplexer_1_out,
       Offset_EX, Offset_MEM, PC_1, PC_1_EX, PC_1_IF, PC_1_MEM, PC_1_OFFSET, PC_1_WB, PC_q, Rdata1_EX,
       Rdata1_MEM, Rdata2_EX, Rdata2_MEM, RESULT_MEM, RESULT_WB, rom_1_data;

  Clock Clock (.out(CLK));
  Multiplexer #(.select(2), .width(32)) multiplexer_1 (
    .in0(PC_1), .in1(PC_1_OFFSET), .in2(Rdata2_MEM), .in3(PC_q), .out(multiplexer_1_out), .sel(PC_SELECT));  // open: en
  Register #(.width(32)) PC (.D(multiplexer_1_out), .en(EN), .Q(PC_q), .clk(CLK));  // open: clr
  Comparator #(.width(4)) comparator_1 (.a(ex_opcode), .b(4'b0011), .eq(comparator_1_eq));  // open: gt, lt
  Comparator #(.width(4)) comparator_2 (.a(Rx_EX), .b(Ry), .eq(comparator_2_eq));  // open: gt, lt
  Comparator #(.width(4)) comparator_3 (.a(Rx_EX), .b(Rz), .eq(comparator_3_eq));  // open: gt, lt
  Comparator #(.width(4)) comparator_4 (.a(opcode), .b(4'b0010), .lt(comparator_4_lt));  // open: gt, eq
  Bit_Extender #(.in_width(32), .out_width(24), .\type ("sign")) bit_extender_1 (.in(PC_q), .out(bit_extender_1_out));
  or or_1 (Squash, PC_SELECT[0], PC_SELECT[1]);
  Adder #(.width(32)) adder_1 (.a(PC_q), .b(32'h1), .out(PC_1));  // open: cin, cout
  and and_1 (and_1_out, comparator_3_eq, comparator_4_lt);
  ROM #(.addrWidth(24), .dataWidth(32)) rom_1 (.addr(bit_extender_1_out), .data(rom_1_data), .sel(EN));
  Register #(.width(1)) register_1 (.D(STALL), .Q(NoOp), .clk(CLK));  // open: en, clr
  or or_2 (or_2_out, comparator_2_eq, and_1_out);
  Multiplexer #(.enable("false")) multiplexer_2 (.in0(1'b1), .in1(1'b0), .out(EN), .sel(STALL));
  and and_2 (STALL, comparator_1_eq, or_2_out);
  ID_RR_controller id_rr_controller_1 (
    .Instruction(if_idrr_buffer_1_inst_out), .Rz(Rz), .Unused(Unused), .Ry(Ry), .Rx(Rx), .Opcode(opcode),
    .REGno2(REGNO2), .Offset(out_11));
  IF_IDRR_Buffer if_idrr_buffer_1 (
    .PC_1(PC_1), .Instruction(rom_1_data), .Clear(Squash), .EN(EN), .Clock(CLK),
    .INST_OUT(if_idrr_buffer_1_inst_out), .PC_1_OUT(PC_1_IF));
  Dual_Ported_Register_File dual_ported_register_file_1 (
    .CLK(CLK), .WrREGNO(REG_WB), .RdREGNO1(Ry), .RdREGNO2(REGNO2), .INPUT(out_5), .OUT1(out_13),
    .OUT2(out_16), .WrEN(WB), .a0(out_10), .a2(out_12), .a1(out_15));
  IDRR_EX_Buffer idrr_ex_buffer_1 (
    .Clear(Squash), .EN(EN), .Clock(CLK), .Offset_IN(out_11), .Rdata1IN(out_9), .Rdata2IN(out_14),
    .OPCODE_IN(opcode), .Rx_In(Rx), .Offset_OUT(idrr_ex_buffer_1_offset_out),
    .PC_OUT(idrr_ex_buffer_1_pc_out), .Rdata1OUT(idrr_ex_buffer_1_rdata1out),
    .Rdata2OUT(idrr_ex_buffer_1_rdata2out), .OPCODE_OUT(idrr_ex_buffer_1_opcode_out),
    .Rx_IN_2(idrr_ex_buffer_1_rx_in_2), .PC_IN(PC_1_IF), .Ry_IN_2(idrr_ex_buffer_1_ry_in_2), .Ry_In(Ry));
  EX_controller ex_controller_1 (
    .Rdata2_Ex(Rdata2_EX), .Offset(Offset_EX), .opcode(ex_opcode), .data_B(out_1), .func(out_3));
  IDRR_EX_buffer_helper idrr_ex_buffer_helper_1 (
    .noop(NoOp), .Offset_out(idrr_ex_buffer_1_offset_out), .Pc__1_out(idrr_ex_buffer_1_pc_out),
    .Rdata1_out(idrr_ex_buffer_1_rdata1out), .Rdata2_out(idrr_ex_buffer_1_rdata2out),
    .opcode(idrr_ex_buffer_1_opcode_out), .Rx(idrr_ex_buffer_1_rx_in_2), .Ry(idrr_ex_buffer_1_ry_in_2),
    .Offset_out_2(Offset_EX), .PC_1_Ourt(PC_1_EX), .Rdata1_Ourt(Rdata1_EX), .Rdata2_Ourt(Rdata2_EX),
    .opcode_out(ex_opcode), .Rx_2(Rx_EX), .Ry_2(Ry_EX));
  Forwarding_unit forwarding_unit_1 (
    .ID_RR_OPCODE(opcode), .IDRR_out1(out_13), .IDRR_Ry(Ry), .IDRR_Rz(REGNO2), .IDRR_out2(out_16),
    .EX_OPCODE(ex_opcode), .EX_Rx(Rx_EX), .EX_Result(out_17), .MEM_OPCODE(OPCODE_MEM), .MEM_Rx(Rx_MEM),
    .MEM_Result(RESULT_MEM), .RAM_Result(out_4), .WB_OPCODE(OPCODE_WB), .WB_Rx(Rx_WB), .WB_Result(out_5),
    .Ry(out_9), .Rz(out_14));
  ALU alu_1 (.FUNC(out_3), .A(Rdata1_EX), .B(out_1), .OUT(out_17));
  Comparator #(.width(32)) comparator_5 (.a(Rdata1_EX), .b(Rdata2_EX), .eq(comparator_5_eq));  // open: gt, lt
  Adder #(.width(32)) adder_2 (.a(PC_1_EX), .b(Offset_EX), .out(adder_2_out));  // open: cin, cout
  EX_MEM_Buffer ex_mem_buffer_1 (
    .EN(1'b1), .Clock(CLK), .Offset_IN(Offset_EX), .Rdata1IN(Rdata1_EX), .Rdata2_IN(Rdata2_EX),
    .Result_IN(out_17), .OPCODE_EX(ex_opcode), .Rx_In(Rx_EX), .Ry_In(Ry_EX), .Offset_OUT(Offset_MEM),
    .Rdata1_OUT(Rdata1_MEM), .Rdata2_OUT(Rdata2_MEM), .Result_Out(RESULT_MEM), .OPCODE_EX_2(OPCODE_MEM),
    .Rx_OUT(Rx_MEM), .Ry_OUT(Ry_MEM), .PC_1_IN(PC_1_EX), .PC_1_OUT(PC_1_MEM), .BRANCH(comparator_5_eq),
    .BRANCH_2(take_branch), .Pc_1_offset(adder_2_out), .Pc_1_offset_2(PC_1_OFFSET));
  MEM_controller mem_controller_1 (
    .clk(CLK), .result_mem(RESULT_MEM), .opcode_mem(OPCODE_MEM), .rdata2__mem(Rdata2_MEM), .RAM_mem(out_4),
    .PC_select(PC_SELECT), .take_branch(take_branch));
  MEM_WB_Buffer mem_wb_buffer_1 (
    .EN(1'b1), .Clock(CLK), .Result_IN(RESULT_MEM), .RAM_OUT(out_4), .OPCODE_IN(OPCODE_MEM), .Rx_In(Rx_MEM),
    .Ry_In(Ry_MEM), .Result_Out(RESULT_WB), .RAM_OUT_2(mem_wb_buffer_1_ram_out_2), .Ry_OUT(Ry_WB),
    .Rx_OUT(Rx_WB), .OPCODE_OUT(OPCODE_WB), .PC_1_IN(PC_1_MEM), .PC_1_OUT(PC_1_WB));
  WB_controller wb_controller_1 (
    .Result_WB(RESULT_WB), .PC_1_WB(PC_1_WB), .RAM_out(mem_wb_buffer_1_ram_out_2), .OPCODE_Wb(OPCODE_WB),
    .WB_data(out_5), .Rx__Wb(Rx_WB), .Ry__Wb(Ry_WB), .REG_WB(REG_WB), .WB(WB));

  // Other names for the same wires on the sheet: a0[31:0] = out_10; a1[31:0] = out_15; a2[31:0] = out_12;
  //   FOUT1[31:0] = out_9; FOUT2[31:0] = out_14; Offset[31:0] = out_11; OPCODE_EX[3:0] = ex_opcode;
  //   OUT1[31:0] = out_13; OUT2[31:0] = out_16; RAM_MEM[31:0] = out_4; RESULT[31:0] = out_17; WB_Data[31:0] = out_5

  // Notes on the sheet:
  //   contents of rom_1 (hex, n*v repeats v):
  //   2400000a 3000000 5000000 23300001 53400001 533ffffd 45000000 25500001 55400001 555ffffc 45000000
  //   500fffff
endmodule

module Dual_Ported_Register_File (
  input  CLK,
  input  WrEN,
  input  [3:0] WrREGNO,
  input  [3:0] RdREGNO1,
  input  [3:0] RdREGNO2,
  input  [31:0] INPUT,
  output [31:0] OUT1,
  output [31:0] OUT2,
  output [31:0] a0,
  output [31:0] a2,
  output [31:0] a1
);

  wire En_a0, En_a1, En_a2, En_a3, En_a4, En_at, En_fp, En_k0, En_ra, En_s0, En_s1, En_s2, En_s3, En_sp,
       En_v0;
  wire [31:0] a3, a4, at, fp, k0, ra, s0, s1, s2, s3, sp, v0, zero;

  Decoder #(.select(4), .disabled(0)) decoder_1 (
    .out1(En_at), .out2(En_v0), .out3(En_a0), .out4(En_a1), .out5(En_a2), .out6(En_a3), .out7(En_a4),
    .out8(En_s0), .out9(En_s1), .out10(En_s2), .out11(En_s3), .out12(En_k0), .out13(En_sp), .out14(En_fp),
    .out15(En_ra), .sel(WrREGNO), .en(WrEN));  // open: out0
  Register #(.width(32)) u_zero (.D(INPUT), .en(1'b0), .Q(zero), .clk(CLK));  // open: clr
  Register #(.width(32)) u_at (.D(INPUT), .en(En_at), .Q(at), .clk(CLK));  // open: clr
  Register #(.width(32)) u_v0 (.D(INPUT), .en(En_v0), .Q(v0), .clk(CLK));  // open: clr
  Register #(.width(32)) u_a0 (.D(INPUT), .en(En_a0), .Q(a0), .clk(CLK));  // open: clr
  Register #(.width(32)) u_a1 (.D(INPUT), .en(En_a1), .Q(a1), .clk(CLK));  // open: clr
  Register #(.width(32)) u_a2 (.D(INPUT), .en(En_a2), .Q(a2), .clk(CLK));  // open: clr
  Register #(.width(32)) u_a3 (.D(INPUT), .en(En_a3), .Q(a3), .clk(CLK));  // open: clr
  Register #(.width(32)) u_a4 (.D(INPUT), .en(En_a4), .Q(a4), .clk(CLK));  // open: clr
  Multiplexer #(.select(4), .width(32), .disabled(0), .enable("false")) multiplexer_1 (
    .in0(zero), .in1(at), .in2(v0), .in3(a0), .in4(a1), .in5(a2), .in6(a3), .in7(a4), .in8(s0), .in9(s1),
    .in10(s2), .in11(s3), .in12(k0), .in13(sp), .in14(fp), .in15(ra), .out(OUT2), .sel(RdREGNO2));
  Register #(.width(32)) u_s0 (.D(INPUT), .en(En_s0), .Q(s0), .clk(CLK));  // open: clr
  Register #(.width(32)) u_s1 (.D(INPUT), .en(En_s1), .Q(s1), .clk(CLK));  // open: clr
  Register #(.width(32)) u_s2 (.D(INPUT), .en(En_s2), .Q(s2), .clk(CLK));  // open: clr
  Register #(.width(32)) u_s3 (.D(INPUT), .en(En_s3), .Q(s3), .clk(CLK));  // open: clr
  Register #(.width(32)) u_k0 (.D(INPUT), .en(En_k0), .Q(k0), .clk(CLK));  // open: clr
  Register #(.width(32)) u_sp (.D(INPUT), .en(En_sp), .Q(sp), .clk(CLK));  // open: clr
  Register #(.width(32)) u_fp (.D(INPUT), .en(En_fp), .Q(fp), .clk(CLK));  // open: clr
  Register #(.width(32)) u_ra (.D(INPUT), .en(En_ra), .Q(ra), .clk(CLK));  // open: clr
  Multiplexer #(.select(4), .width(32), .disabled(0), .enable("false")) multiplexer_2 (
    .in0(zero), .in1(at), .in2(v0), .in3(a0), .in4(a1), .in5(a2), .in6(a3), .in7(a4), .in8(s0), .in9(s1),
    .in10(s2), .in11(s3), .in12(k0), .in13(sp), .in14(fp), .in15(ra), .out(OUT1), .sel(RdREGNO1));

  // Notes on the sheet:
  //   MODIFY AT YOUR OWN RISK
endmodule

// IF/ BUFFER
module IF_IDRR_Buffer (
  input  [31:0] PC_1,
  input  [31:0] Instruction,
  input  Clear,
  input  EN,
  input  Clock,
  output [31:0] PC_1_OUT,
  output [31:0] INST_OUT
);

  Register #(.width(32)) PC (.D(PC_1), .en(EN), .Q(PC_1_OUT), .clk(Clock), .clr(Clear));
  Register #(.width(32)) u_Instruction (.D(Instruction), .en(EN), .Q(INST_OUT), .clk(Clock), .clr(Clear));

  // Other names for the same wires on the sheet: CLK = Clock; CLR = Clear
endmodule

// IDRR/EX BUFFER
module IDRR_EX_Buffer (
  input  Clear,
  input  EN,
  input  Clock,
  input  [31:0] PC_IN,
  input  [31:0] Offset_IN,
  input  [31:0] Rdata1IN,
  input  [31:0] Rdata2IN,
  input  [3:0] OPCODE_IN,
  input  [3:0] Rx_In,
  input  [3:0] Ry_In,
  output [31:0] PC_OUT,
  output [31:0] Offset_OUT,
  output [31:0] Rdata1OUT,
  output [31:0] Rdata2OUT,
  output [3:0] OPCODE_OUT,
  output [3:0] Rx_IN_2,
  output [3:0] Ry_IN_2
);

  Register #(.width(4)) OPCODE (.D(OPCODE_IN), .en(EN), .Q(OPCODE_OUT), .clk(Clock), .clr(Clear));
  Register #(.width(32)) PC (.D(PC_IN), .en(EN), .Q(PC_OUT), .clk(Clock), .clr(Clear));
  Register #(.width(32)) Offset (.D(Offset_IN), .en(EN), .Q(Offset_OUT), .clk(Clock), .clr(Clear));
  Register #(.width(32)) Rdata1 (.D(Rdata1IN), .en(EN), .Q(Rdata1OUT), .clk(Clock), .clr(Clear));
  Register #(.width(32)) Rdata2 (.D(Rdata2IN), .en(EN), .Q(Rdata2OUT), .clk(Clock), .clr(Clear));
  Register #(.width(4)) Rx (.D(Rx_In), .en(EN), .Q(Rx_IN_2), .clk(Clock), .clr(Clear));
  Register #(.width(4)) Ry (.D(Ry_In), .en(EN), .Q(Ry_IN_2), .clk(Clock), .clr(Clear));

  // Other names for the same wires on the sheet: CLK = Clock; CLR = Clear
endmodule

module EX_MEM_Buffer (
  input  EN,
  input  Clock,
  input  [31:0] Offset_IN,
  input  [31:0] Rdata1IN,
  input  [31:0] Rdata2_IN,
  input  [31:0] Result_IN,
  input  [3:0] OPCODE_EX,
  input  [3:0] Rx_In,
  input  [3:0] Ry_In,
  input  [31:0] PC_1_IN,
  input  BRANCH,
  input  [31:0] Pc_1_offset,
  output [31:0] Offset_OUT,
  output [31:0] Rdata1_OUT,
  output [31:0] Rdata2_OUT,
  output [31:0] Result_Out,
  output [3:0] OPCODE_EX_2,
  output [3:0] Rx_OUT,
  output [3:0] Ry_OUT,
  output [31:0] PC_1_OUT,
  output BRANCH_2,
  output [31:0] Pc_1_offset_2
);

  Register #(.width(32)) Rdata2 (.D(Rdata2_IN), .en(EN), .Q(Rdata2_OUT), .clk(Clock));  // open: clr
  Register #(.width(32)) RESULT (.D(Result_IN), .en(EN), .Q(Result_Out), .clk(Clock));  // open: clr
  Register #(.width(4)) OPCODE (.D(OPCODE_EX), .en(EN), .Q(OPCODE_EX_2), .clk(Clock));  // open: clr
  Register #(.width(4)) Ry (.D(Ry_In), .en(EN), .Q(Ry_OUT), .clk(Clock));  // open: clr
  Register #(.width(32)) PC_1 (.D(PC_1_IN), .en(EN), .Q(PC_1_OUT), .clk(Clock));  // open: clr
  Register #(.width(1)) u_BRANCH (.D(BRANCH), .en(EN), .Q(BRANCH_2), .clk(Clock));  // open: clr
  Register #(.width(32)) NEWPC (.D(Pc_1_offset), .en(EN), .Q(Pc_1_offset_2), .clk(Clock));  // open: clr
  Register #(.width(32)) Offset (.D(Offset_IN), .en(EN), .Q(Offset_OUT), .clk(Clock));  // open: clr
  Register #(.width(32)) Rdata1 (.D(Rdata1IN), .en(EN), .Q(Rdata1_OUT), .clk(Clock));  // open: clr
  Register #(.width(4)) Rx (.D(Rx_In), .en(EN), .Q(Rx_OUT), .clk(Clock));  // open: clr

  // Other names for the same wires on the sheet: CLK = Clock
endmodule

// MEM/WB BUFFER
module MEM_WB_Buffer (
  input  EN,
  input  Clock,
  input  [31:0] PC_1_IN,
  input  [31:0] Result_IN,
  input  [31:0] RAM_OUT,
  input  [3:0] OPCODE_IN,
  input  [3:0] Rx_In,
  input  [3:0] Ry_In,
  output [31:0] PC_1_OUT,
  output [31:0] Result_Out,
  output [31:0] RAM_OUT_2,
  output [3:0] OPCODE_OUT,
  output [3:0] Rx_OUT,
  output [3:0] Ry_OUT
);

  Register #(.width(32)) PC_1 (.D(PC_1_IN), .en(EN), .Q(PC_1_OUT), .clk(Clock));  // open: clr
  Register #(.width(32)) RESULT (.D(Result_IN), .en(EN), .Q(Result_Out), .clk(Clock));  // open: clr
  Register #(.width(32)) RAM (.D(RAM_OUT), .en(EN), .Q(RAM_OUT_2), .clk(Clock));  // open: clr
  Register #(.width(4)) OPCODE (.D(OPCODE_IN), .en(EN), .Q(OPCODE_OUT), .clk(Clock));  // open: clr
  Register #(.width(4)) Rx (.D(Rx_In), .en(EN), .Q(Rx_OUT), .clk(Clock));  // open: clr
  Register #(.width(4)) Ry (.D(Ry_In), .en(EN), .Q(Ry_OUT), .clk(Clock));  // open: clr

  // Other names for the same wires on the sheet: CLK = Clock
endmodule

module ALU (
  input  [1:0] FUNC,
  input  [31:0] A,
  input  [31:0] B,
  output [31:0] OUT
);

  wire [31:0] adder_1_out, adder_2_out, nand_1_out, subtractor_1_out;

  Adder #(.width(32)) adder_1 (.a(A), .b(B), .out(adder_1_out), .cin(1'b0));  // open: cout
  assign nand_1_out = ~(A & B);  // NAND_Gate nand_1, 32 bits wide
  Subtractor #(.width(32)) subtractor_1 (.a(A), .b(B), .out(subtractor_1_out), .bin(1'b0));  // open: bout
  Adder #(.width(32)) adder_2 (.a(A), .b({32{1'b0}}), .out(adder_2_out), .cin(1'b1));  // open: cout
  Multiplexer #(.select(2), .width(32), .disabled(0), .enable("false")) multiplexer_1 (
    .in0(adder_1_out), .in1(nand_1_out), .in2(subtractor_1_out), .in3(adder_2_out), .out(OUT), .sel(FUNC));

  // Notes on the sheet:
  //   MODIFY AT YOUR OWN RISK
endmodule

module ID_RR_controller (
  input  [31:0] Instruction,
  output [3:0] Rz,
  output [15:0] Unused,
  output [3:0] Ry,
  output [3:0] Rx,
  output [3:0] Opcode,
  output [3:0] REGno2,
  output [31:0] Offset
);

  wire comparator_1_gt;

  assign Offset = {{12{Instruction[19]}}, Instruction[19:0]};  // Bit_Extender bit_extender_1
  Comparator #(.width(4)) comparator_1 (.a(Instruction[31:28]), .b(4'b0010), .gt(comparator_1_gt));  // open: eq, lt
  Multiplexer #(.width(4), .enable("false")) multiplexer_1 (
    .in0(Instruction[3:0]), .in1(Instruction[27:24]), .out(REGno2), .sel(comparator_1_gt));

  assign Opcode = Instruction[31:28];
  assign Rx = Instruction[27:24];
  assign Ry = Instruction[23:20];
  assign Rz = Instruction[3:0];
  assign Unused = Instruction[19:4];
endmodule

module EX_controller (
  input  [31:0] Rdata2_Ex,
  input  [31:0] Offset,
  input  [3:0] opcode,
  output [31:0] data_B,
  output [1:0] func
);

  wire comparator_1_gt;

  Comparator #(.width(4)) comparator_1 (.a(opcode), .b(4'b0001), .gt(comparator_1_gt), .eq(func[0]));  // open: lt
  Multiplexer #(.width(32), .enable("false")) multiplexer_1 (
    .in0(Rdata2_Ex), .in1(Offset), .out(data_B), .sel(comparator_1_gt));

  assign func[1] = 1'b0;
endmodule

// IDRR/Ex help
module IDRR_EX_buffer_helper (
  input  noop,
  input  [31:0] Offset_out,
  input  [31:0] Pc__1_out,
  input  [31:0] Rdata1_out,
  input  [31:0] Rdata2_out,
  input  [3:0] opcode,
  input  [3:0] Rx,
  input  [3:0] Ry,
  output [31:0] Offset_out_2,
  output [31:0] PC_1_Ourt,
  output [31:0] Rdata1_Ourt,
  output [31:0] Rdata2_Ourt,
  output [3:0] opcode_out,
  output [3:0] Rx_2,
  output [3:0] Ry_2
);

  Multiplexer #(.width(4)) multiplexer_1 (.in0(opcode), .in1(4'b0000), .out(opcode_out), .sel(noop));  // open: en
  Multiplexer #(.width(4)) multiplexer_2 (.in0(Rx), .in1(4'b0000), .out(Rx_2), .sel(noop));  // open: en
  Multiplexer #(.width(4)) multiplexer_3 (.in0(Ry), .in1(4'b0000), .out(Ry_2), .sel(noop));  // open: en
  Multiplexer #(.width(32)) multiplexer_4 (
    .in0(Offset_out), .in1({32{1'b0}}), .out(Offset_out_2), .sel(noop));  // open: en
  Multiplexer #(.width(32), .enable("false")) multiplexer_5 (
    .in0(Pc__1_out), .in1({32{1'b0}}), .out(PC_1_Ourt), .sel(noop));
  Multiplexer #(.width(32), .enable("false")) multiplexer_6 (
    .in0(Rdata1_out), .in1({32{1'b0}}), .out(Rdata1_Ourt), .sel(noop));
  Multiplexer #(.width(32), .enable("false")) multiplexer_7 (
    .in0(Rdata2_out), .in1({32{1'b0}}), .out(Rdata2_Ourt), .sel(noop));
endmodule

// MEM controller
module MEM_controller (
  input  clk,
  input  [31:0] result_mem,
  input  [3:0] opcode_mem,
  input  [31:0] rdata2__mem,
  input  take_branch,
  output [31:0] RAM_mem,
  output [1:0] PC_select
);

  wire comparator_1_eq, comparator_2_eq, comparator_3_eq;
  wire [23:0] bit_extender_1_out;

  Bit_Extender #(.in_width(32), .out_width(24)) bit_extender_1 (.in(result_mem), .out(bit_extender_1_out));
  Comparator #(.width(4)) comparator_1 (.a(4'b0100), .b(opcode_mem), .eq(comparator_1_eq));  // open: gt, lt
  Comparator #(.width(4)) comparator_2 (.a(4'b0011), .b(opcode_mem), .eq(comparator_2_eq));  // open: gt, lt
  Comparator #(.width(4)) comparator_3 (.a(4'b0101), .b(opcode_mem), .eq(comparator_3_eq));  // open: gt, lt
  Comparator #(.width(4)) comparator_4 (.a(4'b0110), .b(opcode_mem), .eq(PC_select[1]));  // open: gt, lt
  and and_1 (PC_select[0], take_branch, comparator_3_eq);
  RAM #(.addrWidth(24), .dataWidth(32), .bus("separate")) ram_1 (
    .addr(bit_extender_1_out), .din(rdata2__mem), .data(RAM_mem), .str(comparator_1_eq), .clk(clk),
    .ld(comparator_2_eq));  // open: sel, clr

  // Notes on the sheet:
  //   BEQ?
  //   jalr?
endmodule

module WB_controller (
  input  [31:0] Result_WB,
  input  [31:0] PC_1_WB,
  input  [31:0] RAM_out,
  input  [3:0] Rx__Wb,
  input  [3:0] Ry__Wb,
  input  [3:0] OPCODE_Wb,
  output [31:0] WB_data,
  output [3:0] REG_WB,
  output WB
);

  wire comparator_2_lt, JALR;
  wire [1:1] comparator_1_eq;

  Comparator #(.width(4)) comparator_1 (.a(OPCODE_Wb), .b(4'b0011), .eq(comparator_1_eq[1]));  // open: gt, lt
  Comparator #(.width(4)) comparator_2 (.a(OPCODE_Wb), .b(4'b0100), .lt(comparator_2_lt));  // open: gt, eq
  Comparator #(.width(4)) comparator_3 (.a(OPCODE_Wb), .b(4'b0110), .eq(JALR));  // open: gt, lt
  Multiplexer #(.select(2), .width(32), .enable("false")) multiplexer_1 (
    .in0(Result_WB), .in1(PC_1_WB), .in2(RAM_out), .out(WB_data), .sel({comparator_1_eq[1], JALR}));  // open: in3
  or or_1 (WB, comparator_2_lt, JALR);
  Multiplexer #(.width(4), .enable("false")) multiplexer_2 (.in0(Rx__Wb), .in1(Ry__Wb), .out(REG_WB), .sel(JALR));
endmodule

module Forwarding_unit (
  input  [3:0] ID_RR_OPCODE,
  input  [31:0] IDRR_out1,
  input  [3:0] IDRR_Ry,
  input  [3:0] IDRR_Rz,
  input  [31:0] IDRR_out2,
  input  [3:0] EX_OPCODE,
  input  [3:0] EX_Rx,
  input  [31:0] EX_Result,
  input  [3:0] MEM_OPCODE,
  input  [3:0] MEM_Rx,
  input  [31:0] MEM_Result,
  input  [31:0] RAM_Result,
  input  [3:0] WB_OPCODE,
  input  [3:0] WB_Rx,
  input  [31:0] WB_Result,
  output [31:0] Ry,
  output [31:0] Rz
);

  wire _0, _0__Ry, _1, _1__Ry, _2__Ry, _2__Rz, _3__Ry, _3__Rz, ADD_NAND, comparator_1_lt, comparator_2_eq,
       comparator_5_lt, comparator_6_eq, comparator_7_lt, comparator_8_eq, ENABLE_EX, ENABLE_MEM, ENABLE_WB,
       EX__ForwardRy, EX__ForwardRz, LW, MEM__ForwardRy, MEM__ForwardRz, Ry_FORWARD_EX_Rx, Ry_FORWARD_MEM_Rx,
       Ry_FORWARD_WB_Rx, Ry_MEM_FORWARD, Rz_FORWARD_EX_Rx, Rz_FORWARD_MEM_Rx, Rz_FORWARD_WB_Rx,
       Rz_MEM_FORWARD, WB__ForwardRy, WB__ForwardRz;
  wire [1:0] Ry_t, Rz_t;
  wire [31:0] MEM_Result_t;

  Comparator #(.width(4)) comparator_1 (.a(EX_OPCODE), .b(4'b0100), .lt(comparator_1_lt));  // open: gt, eq
  Comparator #(.width(4)) comparator_2 (.a(EX_OPCODE), .b(4'b0110), .eq(comparator_2_eq));  // open: gt, lt
  Comparator #(.width(4)) comparator_3 (.a(ID_RR_OPCODE), .b(4'b0010), .lt(ADD_NAND));  // open: gt, eq
  Comparator #(.width(4)) comparator_4 (.a(MEM_OPCODE), .b(4'b0011), .eq(LW));  // open: gt, lt
  Comparator #(.width(4)) comparator_5 (.a(MEM_OPCODE), .b(4'b0100), .lt(comparator_5_lt));  // open: gt, eq
  Comparator #(.width(4)) comparator_6 (.a(MEM_OPCODE), .b(4'b0110), .eq(comparator_6_eq));  // open: gt, lt
  Comparator #(.width(4)) comparator_7 (.a(WB_OPCODE), .b(4'b0100), .lt(comparator_7_lt));  // open: gt, eq
  Comparator #(.width(4)) comparator_8 (.a(WB_OPCODE), .b(4'b0110), .eq(comparator_8_eq));  // open: gt, lt
  or or_1 (ENABLE_EX, comparator_1_lt, comparator_2_eq);
  or or_2 (ENABLE_MEM, comparator_5_lt, comparator_6_eq);
  Multiplexer #(.width(32), .enable("false")) multiplexer_1 (
    .in0(MEM_Result), .in1(RAM_Result), .out(MEM_Result_t), .sel(LW));
  or or_3 (ENABLE_WB, comparator_7_lt, comparator_8_eq);
  Comparator #(.width(4)) comparator_9 (.a(IDRR_Ry), .b(EX_Rx), .eq(EX__ForwardRy));  // open: gt, lt
  Comparator #(.width(4)) comparator_10 (.a(IDRR_Rz), .b(EX_Rx), .eq(EX__ForwardRz));  // open: gt, lt
  Comparator #(.width(4)) comparator_11 (.a(IDRR_Ry), .b(MEM_Rx), .eq(MEM__ForwardRy));  // open: gt, lt
  Comparator #(.width(4)) comparator_12 (.a(IDRR_Rz), .b(MEM_Rx), .eq(MEM__ForwardRz));  // open: gt, lt
  Comparator #(.width(4)) comparator_13 (.a(IDRR_Ry), .b(WB_Rx), .eq(WB__ForwardRy));  // open: gt, lt
  Comparator #(.width(4)) comparator_14 (.a(IDRR_Rz), .b(WB_Rx), .eq(WB__ForwardRz));  // open: gt, lt
  and and_1 (Ry_FORWARD_EX_Rx, ENABLE_EX, EX__ForwardRy);
  and and_2 (Rz_FORWARD_EX_Rx, ENABLE_EX, EX__ForwardRz);
  and and_3 (Rz_FORWARD_MEM_Rx, ENABLE_MEM, MEM__ForwardRz);
  and and_4 (Ry_FORWARD_MEM_Rx, ENABLE_MEM, MEM__ForwardRy);
  and and_5 (Ry_FORWARD_WB_Rx, ENABLE_EX, WB__ForwardRy);
  and and_6 (Rz_FORWARD_WB_Rx, ENABLE_EX, WB__ForwardRz);
  Multiplexer #(.select(2), .width(32), .enable("false")) multiplexer_2 (
    .in0(IDRR_out1), .in1(EX_Result), .in2(MEM_Result_t), .in3(WB_Result), .out(Ry), .sel(Ry_t));
  Multiplexer #(.select(2), .width(32), .enable("false")) multiplexer_3 (
    .in0(IDRR_out2), .in1(EX_Result), .in2(MEM_Result_t), .in3(WB_Result), .out(Rz), .sel(Rz_t));
  Comparator #(.width(3)) comparator_15 (
    .a({Ry_FORWARD_EX_Rx, Ry_FORWARD_MEM_Rx, Ry_FORWARD_WB_Rx}), .b(3'b000), .eq(_0__Ry));  // open: gt, lt
  Comparator #(.width(3)) comparator_16 (
    .a({Ry_FORWARD_EX_Rx, Ry_FORWARD_MEM_Rx, Ry_FORWARD_WB_Rx}), .b(3'b001), .eq(_1__Ry));  // open: gt, lt
  Comparator #(.width(3)) comparator_17 (
    .a({Ry_FORWARD_EX_Rx, Ry_FORWARD_MEM_Rx, Ry_FORWARD_WB_Rx}), .b(3'b010), .eq(_2__Ry));  // open: gt, lt
  Comparator #(.width(3)) comparator_18 (
    .a({Ry_FORWARD_EX_Rx, Ry_FORWARD_MEM_Rx, Ry_FORWARD_WB_Rx}), .b(3'b011), .eq(_3__Ry));  // open: gt, lt
  Comparator #(.width(3)) comparator_19 (
    .a({Rz_FORWARD_EX_Rx, Rz_FORWARD_MEM_Rx, Rz_FORWARD_WB_Rx}), .b(3'b000), .eq(_0));  // open: gt, lt
  Comparator #(.width(3)) comparator_20 (
    .a({Rz_FORWARD_EX_Rx, Rz_FORWARD_MEM_Rx, Rz_FORWARD_WB_Rx}), .b(3'b001), .eq(_1));  // open: gt, lt
  Comparator #(.width(3)) comparator_21 (
    .a({Rz_FORWARD_EX_Rx, Rz_FORWARD_MEM_Rx, Rz_FORWARD_WB_Rx}), .b(3'b010), .eq(_2__Rz));  // open: gt, lt
  Comparator #(.width(3)) comparator_22 (
    .a({Rz_FORWARD_EX_Rx, Rz_FORWARD_MEM_Rx, Rz_FORWARD_WB_Rx}), .b(3'b011), .eq(_3__Rz));  // open: gt, lt
  assign Ry_t = _0__Ry ? 2'b00 : 2'bz;  // Controlled_Buffer controlled_buffer_1
  assign Ry_t = Ry_FORWARD_EX_Rx ? 2'b01 : 2'bz;  // Controlled_Buffer controlled_buffer_2
  assign Ry_t = Ry_MEM_FORWARD ? 2'b10 : 2'bz;  // Controlled_Buffer controlled_buffer_3
  assign Ry_t = _1__Ry ? 2'b11 : 2'bz;  // Controlled_Buffer controlled_buffer_4
  or or_4 (Ry_MEM_FORWARD, _2__Ry, _3__Ry);
  assign Rz_t = _0 ? 2'b00 : 2'bz;  // Controlled_Buffer controlled_buffer_5
  assign Rz_t = Rz_FORWARD_EX_Rx ? 2'b01 : 2'bz;  // Controlled_Buffer controlled_buffer_6
  assign Rz_t = Rz_MEM_FORWARD ? 2'b10 : 2'bz;  // Controlled_Buffer controlled_buffer_7
  assign Rz_t = _1 ? 2'b11 : 2'bz;  // Controlled_Buffer controlled_buffer_8
  or or_5 (Rz_MEM_FORWARD, _2__Rz, _3__Rz);

  // Other names for the same wires on the sheet: IDDR_Rout1[31:0] = IDRR_out1; IDDR_Rout2[31:0] = IDRR_out2;
  //   IDDR_Ry[3:0] = IDRR_Ry; IDDR_Rz[3:0] = IDRR_Rz
endmodule
